# Fritzing sketch Generic CPS 498 Looper Schematic (saved by Fritzing 0.9.6b)
breadboards: 1

parts:
  U1 = ESP32S-HiLetgo [part_number=ESP32-DevBoard]
  Part1 = Breadboard Power Supply Board SMD
  Relay_CH2 = KY-019 5V Relay Module [package="Breakout board"]
  1/4"_Guitar_Jack_out_CH2 = AMPHENOL - ACJS-MHDR [package=ACJS-MHDR]
  1/4"_Guitar_Jack_In_CH2 = AMPHENOL - ACJS-MHDR [package=ACJS-MHDR]
  Relay_CH3 = KY-019 5V Relay Module [package="Breakout board"]
  1/4"_Guitar_Jack_out_CH3 = AMPHENOL - ACJS-MHDR [package=ACJS-MHDR]
  1/4"_Guitar_Jack_In_CH3 = AMPHENOL - ACJS-MHDR [package=ACJS-MHDR]
  Relay_CH4 = KY-019 5V Relay Module [package="Breakout board"]
  1/4"_Guitar_Jack_In_CH4 = AMPHENOL - ACJS-MHDR [package=ACJS-MHDR]
  1/4"_Guitar_Jack_out_CH4 = AMPHENOL - ACJS-MHDR [package=ACJS-MHDR]
  Relay_CH6 = KY-019 5V Relay Module [package="Breakout board"]
  Relay_CH8 = KY-019 5V Relay Module [package="Breakout board"]
  Relay_CH5 = KY-019 5V Relay Module [package="Breakout board"]
  Relay_CH7 = KY-019 5V Relay Module [package="Breakout board"]
  1/4"_Guitar_Jack_out_CH7 = AMPHENOL - ACJS-MHDR [package=ACJS-MHDR]
  1/4"_Guitar_Jack_In_CH8 = AMPHENOL - ACJS-MHDR [package=ACJS-MHDR]
  1/4"_Guitar_Jack_In_CH6 = AMPHENOL - ACJS-MHDR [package=ACJS-MHDR]
  1/4"_Guitar_Jack_out_CH8 = AMPHENOL - ACJS-MHDR [package=ACJS-MHDR]
  1/4"_Guitar_Jack_In_CH7 = AMPHENOL - ACJS-MHDR [package=ACJS-MHDR]
  1/4"_Guitar_Jack_In_CH5 = AMPHENOL - ACJS-MHDR [package=ACJS-MHDR]
  1/4"_Guitar_Jack_out_CH6 = AMPHENOL - ACJS-MHDR [package=ACJS-MHDR]
  1/4"_Guitar_Jack_out_CH5 = AMPHENOL - ACJS-MHDR [package=ACJS-MHDR]
  1/4"_Guitar_Jack_Circuit_Out = AMPHENOL - ACJS-MHDR [package=ACJS-MHDR]
  1/4"_Guitar_Jack_Circuit_In = AMPHENOL - ACJS-MHDR [package=ACJS-MHDR]
  S1 = SWITCH-MOMENTARY-2 [package=tactile-switch-1101ne]
  S2 = SWITCH-MOMENTARY-2 [package=tactile-switch-1101ne]
  S3 = SWITCH-MOMENTARY-2 [package=tactile-switch-1101ne]
  S4 = SWITCH-MOMENTARY-2 [package=tactile-switch-1101ne]
  S5 = SWITCH-MOMENTARY-2 [package=tactile-switch-1101ne]
  S6 = SWITCH-MOMENTARY-2 [package=tactile-switch-1101ne]
  DS2Y-5-DC5V2 = DS2Y-5-DC5V [part_number=DS2Y-5-DC5V]
  1/4"_Guitar_Jack_In_CH9 = AMPHENOL - ACJS-MHDR [package=ACJS-MHDR]
  1/4"_Guitar_Jack_out_CH9 = AMPHENOL - ACJS-MHDR [package=ACJS-MHDR]
  J1 = Power Jack [package=power_jack_slot]

nets:
  Btn3: U1.GPIO36, S3.2
  Btn4: U1.GPIO39, S4.2
  Btn1: U1.GPIO34, S1.2
  Btn2: U1.GPIO35, S2.2
  Relay 6: U1.GPIO25, Relay_CH6.S
  Relay 7: U1.GPIO26, Relay_CH7.S
  Relay 3: U1.GPIO27, U1.GPIO21, Relay_CH3.S
  Btn5: U1.GPIO14, S5.2
  GND: U1.GND, Part1.GND, Relay_CH2.-, 1/4"_Guitar_Jack_out_CH2.Sleeve_(4), 1/4"_Guitar_Jack_In_CH2.Sleeve_(4), Relay_CH3.-, 1/4"_Guitar_Jack_out_CH3.Sleeve_(4), 1/4"_Guitar_Jack_In_CH3.Sleeve_(4), Relay_CH4.-, 1/4"_Guitar_Jack_In_CH4.Sleeve_(4), 1/4"_Guitar_Jack_out_CH4.Sleeve_(4), Relay_CH6.-, Relay_CH8.-, Relay_CH5.-, Relay_CH7.-, 1/4"_Guitar_Jack_out_CH7.Sleeve_(4), 1/4"_Guitar_Jack_In_CH8.Sleeve_(4), 1/4"_Guitar_Jack_In_CH6.Sleeve_(4), 1/4"_Guitar_Jack_out_CH8.Sleeve_(4), 1/4"_Guitar_Jack_In_CH7.Sleeve_(4), 1/4"_Guitar_Jack_In_CH5.Sleeve_(4), 1/4"_Guitar_Jack_out_CH6.Sleeve_(4), 1/4"_Guitar_Jack_out_CH5.Sleeve_(4), 1/4"_Guitar_Jack_Circuit_Out.Sleeve_(4), 1/4"_Guitar_Jack_Circuit_In.Sleeve_(4), S1.1, S2.1, S3.1, S4.1, S5.1, S6.1, DS2Y-5-DC5V2.1_+, J1.GNDBREAK, J1.GND
  5V: U1.VIN, Part1.VCC, Relay_CH2.+, Relay_CH3.+, Relay_CH4.+, Relay_CH6.+, Relay_CH8.+, Relay_CH5.+, Relay_CH7.+
  Btn6: U1.GPIO16, S6.2
  Relay 1: U1.GPIO18, DS2Y-5-DC5V2.16_-
  Relay 2: U1.GPIO19, Relay_CH2.S
  Relay 4: U1.GPIO22, Relay_CH4.S
  Relay 5: U1.GPIO23, Relay_CH5.S
  N1: Part1.VIN, J1.PWR
  Relay 3 Signal In: Relay_CH2.NC, 1/4"_Guitar_Jack_In_CH2.Ring_(2), 1/4"_Guitar_Jack_In_CH2.Tip_(3), Relay_CH3.Common
  Relay 2 Signal In: Relay_CH2.Common, DS2Y-5-DC5V2.8_N.O., 1/4"_Guitar_Jack_In_CH9.Ring_(5), 1/4"_Guitar_Jack_In_CH9.Tip_(6)
  N2: Relay_CH2.NO, 1/4"_Guitar_Jack_out_CH2.Ring_(2), 1/4"_Guitar_Jack_out_CH2.Tip_(3)
  Relay 4 Signal In: Relay_CH3.NC, 1/4"_Guitar_Jack_In_CH3.Ring_(2), 1/4"_Guitar_Jack_In_CH3.Tip_(3), Relay_CH4.Common
  N3: Relay_CH3.NO, 1/4"_Guitar_Jack_out_CH3.Ring_(2), 1/4"_Guitar_Jack_out_CH3.Tip_(3)
  Relay 5 Signal In: Relay_CH4.NC, 1/4"_Guitar_Jack_In_CH4.Ring_(2), 1/4"_Guitar_Jack_In_CH4.Tip_(3), Relay_CH5.Common
  N4: Relay_CH4.NO, 1/4"_Guitar_Jack_out_CH4.Ring_(2), 1/4"_Guitar_Jack_out_CH4.Tip_(3)
  Relay 7 Signal In: Relay_CH6.NC, Relay_CH7.Common, 1/4"_Guitar_Jack_In_CH6.Ring_(2), 1/4"_Guitar_Jack_In_CH6.Tip_(3)
  Relay 6 Signal In: Relay_CH6.Common, Relay_CH5.NC, 1/4"_Guitar_Jack_In_CH5.Ring_(2), 1/4"_Guitar_Jack_In_CH5.Tip_(3)
  N5: Relay_CH6.NO, 1/4"_Guitar_Jack_out_CH6.Ring_(2), 1/4"_Guitar_Jack_out_CH6.Tip_(3)
  Relay 8: Relay_CH8.S
  Switcher Out: Relay_CH8.NC, 1/4"_Guitar_Jack_In_CH8.Ring_(2), 1/4"_Guitar_Jack_In_CH8.Tip_(3), 1/4"_Guitar_Jack_Circuit_Out.Ring_(2), 1/4"_Guitar_Jack_Circuit_Out.Tip_(3)
  Relay 8 Signal In: Relay_CH8.Common, Relay_CH7.NC, 1/4"_Guitar_Jack_In_CH7.Ring_(2), 1/4"_Guitar_Jack_In_CH7.Tip_(3)
  N6: Relay_CH8.NO, 1/4"_Guitar_Jack_out_CH8.Ring_(2), 1/4"_Guitar_Jack_out_CH8.Tip_(3)
  N7: Relay_CH5.NO, 1/4"_Guitar_Jack_out_CH5.Ring_(2), 1/4"_Guitar_Jack_out_CH5.Tip_(3)
  N8: Relay_CH7.NO, 1/4"_Guitar_Jack_out_CH7.Ring_(2), 1/4"_Guitar_Jack_out_CH7.Tip_(3)
  Switcher Input: 1/4"_Guitar_Jack_Circuit_In.Ring_(2), 1/4"_Guitar_Jack_Circuit_In.Tip_(3), DS2Y-5-DC5V2.4_COM
  N9: DS2Y-5-DC5V2.6_N.C., 1/4"_Guitar_Jack_out_CH9.Ring_(5), 1/4"_Guitar_Jack_out_CH9.Tip_(6)
  Switcher Input GND: DS2Y-5-DC5V2.13_COM
  N10: DS2Y-5-DC5V2.11_N.C., 1/4"_Guitar_Jack_out_CH9.Sleeve_(1)
  Relay 2 Signal In GND: DS2Y-5-DC5V2.9_N.O., 1/4"_Guitar_Jack_In_CH9.Sleeve_(1)
  N11: 1/4"_Guitar_Jack_In_CH9.Ring_(2), 1/4"_Guitar_Jack_In_CH9.Tip_(3)
  N12: 1/4"_Guitar_Jack_out_CH9.Ring_(2), 1/4"_Guitar_Jack_out_CH9.Tip_(3)

custom parts:
  ESP32S-HiLetgo: HiLetgo ESP-WROOM-32 ESP32 ESP-32S Development Board 2.4GHz Dual-Mode WiFi + Bluetooth Dual Cores Microcontroller The ESP32 integrated with Antenna switches, RF Balun, power amplifiers, low-noise amplifiers, filters, and management modules, and the entire solution occupies the least area of PCB. 2.4 GHz Wi-Fi plus Bluetooth dual-mode chip, with TSMC Ultra-low power consumption 40nm technology,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
  KY-019 5V Relay Module: KY-019 5V Relay module, used to control AC circuits. (Special thanks to vanepp for fixing the PCB holes and other errors)
